# Fritzing sketch Lecture_etat_interrupteur (saved by Fritzing 0.9.1b)
circuit board: 8.46667cm x 5.64444cm
breadboards: 1

parts:
  Composant1 = Arduino Mega 2560 (Rev3)
  S1 = Pushbutton [package=THT]
  S2 = Pushbutton [package=THT]
  S3 = Pushbutton [package=THT]

nets:
  N1: Composant1.GND, S1.leg1, S2.leg1, S3.leg1
  N2: Composant1.D50, S1.leg0
  N3: Composant1.D51, S2.leg0
  N4: Composant1.D52, S3.leg0

// code stored in the sketch: Lecture_etat_interrupteur.ino
//define 
int bouton1 = 50;
int bouton2 = 51;
int bouton3 = 52;
int led = 13;


void setup() {
  // initialize serial communication at 9600 bits per second:
  Serial.begin(9600);
  // make the pushbutton's pin an input:
  pinMode(bouton1, INPUT_PULLUP);
  pinMode(bouton2, INPUT_PULLUP);
  pinMode(bouton3, INPUT_PULLUP);
  pinMode(led, OUTPUT);
}

void loop() {
  

 int buttonState1 = digitalRead(bouton1);
 int buttonState2 = digitalRead(bouton2);
 int buttonState3 = digitalRead(bouton3);
  
  // print out the state of buttons  
  Serial.print("Bouton1="); 
  Serial.print("\t");
  Serial.println(buttonState1);
  Serial.print("Bouton2="); 
  Serial.print("\t");
  Serial.println(buttonState2);
  Serial.print("Bouton3="); 
  Serial.print("\t");
  Serial.println(buttonState3);
  
  //delays for human read.
  delay(200);
}
