# Fritzing sketch feux_tricolor (saved by Fritzing 0.9.1b)
breadboards: 1

parts:
  Composant1 = Arduino Uno (Rev3)
  LED1 = LED - 5mm [color="Red (633nm)" package="5 mm [THT]"]
  LED2 = LED - 5mm [color="Orange (612nm)" package="5 mm [THT]"]
  LED3 = LED - 5mm [color="Green (570nm)" package="5 mm [THT]"]
  LED4 = LED - 5mm [color="Red (633nm)" package="5 mm [THT]"]
  LED5 = LED - 5mm [color="Orange (612nm)" package="5 mm [THT]"]
  LED6 = LED - 5mm [color="Green (570nm)" package="5 mm [THT]"]
  R1 = Resistor [tolerance=±5% resistance=680 package=THT]
  R2 = Resistor [tolerance=±5% resistance=680 package=THT]
  R3 = Resistor [tolerance=±5% resistance=680 package=THT]
  R4 = Resistor [tolerance=±5% resistance=680 package=THT]
  R5 = Resistor [tolerance=±5% resistance=680 package=THT]
  R6 = Resistor [tolerance=±5% resistance=680 package=THT]
  R7 = Resistor [tolerance=±5% resistance=680 package=THT]
  R8 = Resistor [tolerance=±5% resistance=680 package=THT]
  S1 = Toggle Switch [package=THT]

nets:
  N1: Composant1.D8, LED5.cathode
  N2: Composant1.D9_PWM, LED4.cathode
  N3: Composant1.GND, R1.Pin_0, R2.Pin_0, R3.Pin_0, R4.Pin_0, R5.Pin_0, R6.Pin_0, R7.Pin_0, R8.Pin_0
  N4: Composant1.D2, R8.Pin_1, S1.L2
  N5: Composant1.D3_PWM, R7.Pin_1, S1.L1
  N6: Composant1.D4, LED3.cathode
  N7: Composant1.D5_PWM, LED2.cathode
  N8: Composant1.D6_PWM, LED1.cathode
  N9: Composant1.D7, LED6.cathode
  N10: Composant1.5V, S1.COM
  N11: LED1.anode, R3.Pin_1
  N12: LED2.anode, R2.Pin_1
  N13: LED3.anode, R1.Pin_1
  N14: LED4.anode, R6.Pin_1
  N15: LED5.anode, R5.Pin_1
  N16: LED6.anode, R4.Pin_1
